# Fritzing sketch Schema (saved by Fritzing 0.9.3b)

parts:
  STM32F103C8 = STM32F103C8T6 blue mini board  # not connected
  ENCODER = Rotary Encoder with switch (KY-040) [part_number=KY-040]
  L298N = L298N DC motor driver
  12V_Adapter = 2.1mm DC Barrel Jack
  DC_Motor_M2 = DC Motor  # not connected

nets:
  N1: ENCODER.GND, ENCODER.+
  N2: L298N.12V, 12V_Adapter.center
  N3: L298N.GND, 12V_Adapter.sleeve

custom parts:
  STM32F103C8T6 blue mini board: Generic Blue Pill microcomputer module, available from Ebay and others. CPU STM32F103C8 72Mhz Flash: 64 KB/128 KB RAM: 20KB.
  Rotary Encoder with switch (KY-040): A Rotary Encoder with switch
  L298N DC motor driver: 2x DC motor driver with 78M05 positive voltage regulator (7..35 V) L298N: max 46 V, 2 A Set 5 V Enable jumper to enable 5 V regultor (needed for the L298N) and +5 V output at screw terminal or supply external +5 V at screw terminal Set ENA and/or ENB to +5 V to enable motor permanently or supply ENA and/or ENB with PWM signal IN1 and IN2 set rotation directory for motor A (OUT1/OUT2) IN2 and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
  2.1mm DC Barrel Jack: 2.1mm DC Barrel Jack with Thru-Hole Connectors (breadboardable)
